# Fritzing sketch wemos_ident (saved by Fritzing 0.9.2b)

parts:
  WeMos_D1_R1 = WeMos D1 R2
  Module1 = Boladge HMC5883L Compass Module
  LED1 = LED - 3mm [color="Green (570nm)" package="3 mm [THT]"]
  LED2 = LED - 3mm [color="Yellow (595nm)" package="3 mm [THT]"]
  LED3 = LED - 3mm [color="Red (660nm)" package="3 mm [THT]"]
  Part1 = JeePlug experimenter's board

nets:
  N1: WeMos_D1_R1.(D5), Part1.N$45
  N2: WeMos_D1_R1.(D6), Part1.N$64
  N3: WeMos_D1_R1.(D7), Part1.N$57
  N4: WeMos_D1_R1.GND#15, Part1.N$53
  N5: WeMos_D1_R1.D14, Module1.SDA
  N6: WeMos_D1_R1.D15, Module1.SCL
  N7: WeMos_D1_R1.GND#20, Module1.GND
  3.3V: WeMos_D1_R1.3.3V, Module1.VCC
  N8: LED1.cathode, Part1.N$55
  N9: LED1.anode, Part1.N$7
  N10: LED2.cathode, Part1.N$23
  N11: LED2.anode, Part1.N$31
  N12: LED3.cathode, Part1.N$39
  N13: LED3.anode, Part1.N$47
  N14: Part1.N$10, Part1.N$15
  N15: Part1.N$16, Part1.N$32, Part1.N$48, Part1.N$54
  N16: Part1.N$25, Part1.N$63
  N17: Part1.N$40, Part1.N$46

custom parts:
  WeMos D1 R2: The D1 R2 is a mini wifi board based on the ESP-8266EX.
  Boladge HMC5883L Compass Module: Cheap digital compass module
